// Logisim project LAB1_MAC.circ as structural Verilog: 3 circuits, main circuit add1bit
module add1bit (
  input  A0,
  input  B0,
  input  C0,
  output C1,
  output S0
);

  wire and_1_out, and_2_out, and_3_out, or_1_out, or_2_out, xor_1_out;

  xor xor_1 (xor_1_out, A0, B0);
  and and_1 (and_1_out, A0, B0);
  and and_2 (and_2_out, A0, C0);
  and and_3 (and_3_out, B0, C0);
  xor xor_2 (S0, xor_1_out, C0);
  or or_1 (or_1_out, and_1_out, and_2_out);
  or or_2 (or_2_out, and_2_out, and_3_out);
  or or_3 (C1, or_1_out, or_2_out);
endmodule

module add8bit (
  input  [7:0] in_1,
  input  [7:0] in_2,
  input  c0,
  output c8,
  output [7:0] out_5
);

  wire add1bit_1_c1, add1bit_2_c1, add1bit_3_c1, add1bit_4_c1, add1bit_5_c1, add1bit_6_c1, add1bit_7_c1;

  add1bit add1bit_1 (.A0(in_2[0]), .B0(in_1[0]), .C0(c0), .C1(add1bit_1_c1), .S0(out_5[0]));
  add1bit add1bit_2 (.A0(in_2[1]), .B0(in_1[1]), .C0(add1bit_1_c1), .C1(add1bit_2_c1), .S0(out_5[1]));
  add1bit add1bit_3 (.A0(in_2[3]), .B0(in_1[3]), .C0(add1bit_2_c1), .C1(add1bit_3_c1), .S0(out_5[2]));
  add1bit add1bit_4 (.A0(in_2[4]), .B0(in_1[4]), .C0(add1bit_3_c1), .C1(add1bit_4_c1), .S0(out_5[3]));
  add1bit add1bit_5 (.A0(in_2[4]), .B0(in_1[4]), .C0(add1bit_4_c1), .C1(add1bit_5_c1), .S0(out_5[4]));
  add1bit add1bit_6 (.A0(in_2[5]), .B0(in_1[5]), .C0(add1bit_5_c1), .C1(add1bit_6_c1), .S0(out_5[5]));
  add1bit add1bit_7 (.A0(in_2[6]), .B0(in_1[6]), .C0(add1bit_6_c1), .C1(add1bit_7_c1), .S0(out_5[6]));
  add1bit add1bit_8 (.A0(in_2[7]), .B0(in_1[7]), .C0(add1bit_7_c1), .C1(c8), .S0(out_5[7]));

  // Other names for the same wires on the sheet: b0 = in_1[0]; b1 = in_1[1]; b2 = in_1[2]; b3 = in_1[3]; b4 = in_1[4];
  //   b5 = in_1[5]; b6 = in_1[6]; b7 = in_1[7]; a0 = in_2[0]; a1 = in_2[1]; a2 = in_2[2]; a3 = in_2[3]; a4 = in_2[4];
  //   a5 = in_2[5]; a6 = in_2[6]; a7 = in_2[7]; s0 = out_5[0]; s1 = out_5[1]; s2 = out_5[2]; s3 = out_5[3];
  //   s4 = out_5[4]; s5 = out_5[5]; s6 = out_5[6]; s7 = out_5[7]
endmodule

module ALU (
  input  [3:0] status,
  input  [2:0] OP,
  input  [7:0] b,
  input  [7:0] a,
  output [7:0] result
);

  wire and_4_out, and_5_out, is_substraction, not_3_out, not_4_out, not_5_out, not_6_out, not_7_out;
  wire [7:0] a_and_b, a_lshift_b, a_or_b, a_plus_b, a_rshift_b, a_xor_b, multiplexer_2_out, not_a, not_b;

  assign not_b = ~b;  // NOT_Gate not_1, 8 bits wide
  assign not_a = ~a;  // NOT_Gate not_2, 8 bits wide
  Multiplexer #(.select(3), .width(8)) multiplexer_1 (
    .in0(a_plus_b), .in1(a_plus_b), .in2(a_and_b), .in3(a_or_b), .in4(not_a), .in5(a_xor_b),
    .in6(a_lshift_b), .in7(a_rshift_b), .out({status[0], result[6:0]}), .sel(OP));
  assign a_xor_b = a ^ b;  // XOR_Gate xor_1, 8 bits wide
  assign a_and_b = a & b;  // AND_Gate and_1, 8 bits wide
  assign a_or_b = a | b;  // OR_Gate or_1, 8 bits wide
  Multiplexer #(.width(8)) multiplexer_2 (.in0(b), .in1(not_b), .out(multiplexer_2_out), .sel(is_substraction));
  Shifter shifter_1 (.in(a), .\dist (b[2:0]), .out(a_lshift_b));
  Shifter #(.shift("lr")) shifter_2 (.in(a), .\dist (b[2:0]), .out(a_rshift_b));
  and and_2 (status[1], result[0], result[1], result[2], result[3], result[4], result[5], result[6], status[0]);
  add8bit add8bit_1 (.in_1(multiplexer_2_out), .in_2(a), .c0(is_substraction), .c8(status[3]), .out_5(a_plus_b));
  not not_3 (not_3_out, a[7]);
  not not_4 (not_4_out, b[7]);
  not not_5 (not_5_out, status[0]);
  not not_6 (not_6_out, OP[1]);
  not not_7 (not_7_out, OP[2]);
  and and_3 (is_substraction, not_6_out, not_7_out, OP[0]);
  and and_4 (and_4_out, not_3_out, not_4_out, status[0]);
  and and_5 (and_5_out, a[7], b[7], not_5_out);
  or or_2 (status[2], and_4_out, and_5_out);

  assign result[7] = status[0];

  // Other names for the same wires on the sheet: r7 = status[0]; is_zero = status[1]; overflow = status[2];
  //   carry = status[3]
endmodule
